# Fritzing sketch Breadboard_PerlerPrinter (saved by Fritzing 0.9.3b)
breadboards: 2

parts:
  Part1 = EasyDriver_v44
  Part2 = EasyDriver_v44
  Part3 = Arduino Uno (Rev3)
  Part4 = Thumb Joystick
  Part5 = Thumb Joystick
  Part6 = EasyDriver_v44  # not connected
  Z_Axis_Grab = Stepper Motor - Bipolar  # not connected
  Y_Axis_Move = Stepper Motor - Bipolar  # not connected
  X_Axis_Move = Stepper Motor - Bipolar  # not connected
  Z_Axis_Move = Basic Servo  # not connected

nets:
  GND: Part1.GND, Part2.GND, Part3.GND, Part4.GND, Part5.GND
  N1: Part1.STEP, Part3.D4
  N2: Part1.DIR, Part3.D5_PWM
  N3: Part2.STEP, Part3.D2
  N4: Part2.DIR, Part3.D3_PWM
  N5: Part3.A0, Part4.VERT
  N6: Part3.A1, Part4.HORZ
  N7: Part3.A2, Part5.VERT
  N8: Part3.A3, Part5.HORZ
  N9: Part3.D8, Part5.SEL
  VCC: Part3.5V, Part4.VCC, Part5.VCC
